// Logisim project alu.circ as structural Verilog: 15 circuits, main circuit main
module main (
  input  [3:0] in_1,
  input  in_2,
  input  [3:0] in_3,
  input  [3:0] in_4,
  output [3:0] out_5,
  output [3:0] out_6,
  output [3:0] out_7,
  output [3:0] out_8,
  output [3:0] out_9,
  output [3:0] out_10,
  output [3:0] out_11,
  output [3:0] out_12,
  output [3:0] out_13
);

  wire [3:0] n4_bit_and_1_output, n4_bit_and_2_output, n4_bit_and_3_output, n4_bit_and_4_output,
       n4_bit_and_5_output, n4_bit_and_6_output, n4_bit_and_7_output, n4_bit_and_8_output,
       n4_bit_and_9_output, n4_bit_and_11_output, n4_bit_and_12_output, n4_bit_and_13_output,
       n4_bit_and_14_output, n4_bit_and_15_output;
  wire [3:3] n4_to_16_decoder_1_out_3_2, n4_to_16_decoder_1_out_3_3, n4_to_16_decoder_1_out_3_4,
       n4_to_16_decoder_1_out_3_5, n4_to_16_decoder_1_out_3_6;
  wire [15:5] n4_to_16_decoder_1_out_3;

  _4_bit_and u_4_bit_and_1 (.A_In(in_3), .B_In({4{n4_to_16_decoder_1_out_3[8]}}), .Output(n4_bit_and_1_output));
  _4_to_16_decoder u_4_to_16_decoder_1 (
    .Data_In(in_2), .Address__operation(in_1),
    .out_3({n4_to_16_decoder_1_out_3, n4_to_16_decoder_1_out_3_2[3], n4_to_16_decoder_1_out_3_3[3], n4_to_16_decoder_1_out_3_4[3], n4_to_16_decoder_1_out_3_5[3], n4_to_16_decoder_1_out_3_6[3]}));
  _4_bit_and u_4_bit_and_2 (.A_In(in_4), .B_In({4{n4_to_16_decoder_1_out_3[8]}}), .Output(n4_bit_and_2_output));
  _4_bit_full_adder u_4_bit_full_adder_1 (
    .A_In(n4_bit_and_1_output), .B_In(n4_bit_and_2_output), .Output(out_5), .Carry_In(1'b0));  // open: Carry_Out
  _4_bit_and u_4_bit_and_3 (.A_In(in_3), .B_In({4{n4_to_16_decoder_1_out_3[7]}}), .Output(n4_bit_and_3_output));
  _4_bit_subtractor u_4_bit_subtractor_1 (
    .B_In(n4_bit_and_4_output), .A_In(n4_bit_and_3_output), .Output(out_6));  // open: Overflow___Underflow
  _4_bit_and u_4_bit_and_4 (.A_In(in_4), .B_In({4{n4_to_16_decoder_1_out_3[7]}}), .Output(n4_bit_and_4_output));
  _4_bit_and u_4_bit_and_5 (.A_In(in_3), .B_In({4{n4_to_16_decoder_1_out_3[6]}}), .Output(n4_bit_and_5_output));
  _4_bit_increment u_4_bit_increment_1 (.Input(n4_bit_and_5_output), .Output(out_7));  // open: Carry_Out
  _4_bit_and u_4_bit_and_6 (.A_In(in_3), .B_In({4{n4_to_16_decoder_1_out_3[5]}}), .Output(n4_bit_and_6_output));
  _4_bit_decrementer u_4_bit_decrementer_1 (.Input(n4_bit_and_6_output), .Output(out_8));  // open: Carry_Out
  _4_bit_and u_4_bit_and_7 (.A_In(in_3), .B_In({4{n4_to_16_decoder_1_out_3_2[3]}}), .Output(n4_bit_and_7_output));
  _4_bit_right_shift u_4_bit_right_shift_1 (.Input(n4_bit_and_7_output), .Output(out_9));
  _4_bit_and u_4_bit_and_8 (.A_In(in_3), .B_In({4{n4_to_16_decoder_1_out_3_3[3]}}), .Output(n4_bit_and_8_output));
  _4_bit_left_shift u_4_bit_left_shift_1 (.Input(n4_bit_and_8_output), .Output(out_10));
  _4_bit_and u_4_bit_and_9 (.A_In(in_3), .B_In({4{n4_to_16_decoder_1_out_3_4[3]}}), .Output(n4_bit_and_9_output));
  _4_bit_and u_4_bit_and_10 (.A_In(n4_bit_and_9_output), .B_In(n4_bit_and_11_output), .Output(out_11));
  _4_bit_and u_4_bit_and_11 (.A_In(in_4), .B_In({4{n4_to_16_decoder_1_out_3_4[3]}}), .Output(n4_bit_and_11_output));
  _4_bit_and u_4_bit_and_12 (.A_In(in_3), .B_In({4{n4_to_16_decoder_1_out_3_5[3]}}), .Output(n4_bit_and_12_output));
  _4_bit_and u_4_bit_and_13 (.A_In(in_4), .B_In({4{n4_to_16_decoder_1_out_3_5[3]}}), .Output(n4_bit_and_13_output));
  _4_bit_or u_4_bit_or_1 (.A_In(n4_bit_and_12_output), .B_In(n4_bit_and_13_output), .Output(out_12));
  _4_bit_and u_4_bit_and_14 (.A_In(in_3), .B_In({4{n4_to_16_decoder_1_out_3_6[3]}}), .Output(n4_bit_and_14_output));
  _4_bit_and u_4_bit_and_15 (.A_In(in_4), .B_In({4{n4_to_16_decoder_1_out_3_6[3]}}), .Output(n4_bit_and_15_output));
  _4_bit_xor u_4_bit_xor_1 (.A_In(n4_bit_and_14_output), .B_In(n4_bit_and_15_output), .Output(out_13));
endmodule

// 1-bit Half\nAdder
module _1_bit_half_adder (
  input  A_In,
  input  B_In,
  output Sum_Out,
  output Carry_Out
);

  xor xor_1 (Sum_Out, A_In, B_In);
  and and_1 (Carry_Out, A_In, B_In);
endmodule

// 4-Bit\nFull Adder
module _4_bit_full_adder (
  input  [3:0] A_In,
  input  [3:0] B_In,
  input  Carry_In,
  output Carry_Out,
  output [3:0] Output
);

  wire n1_bit_full_adder_2_carry_out, n1_bit_full_adder_3_carry_out, n1_bit_full_adder_4_carry_out;

  _1_bit_full_adder u_1_bit_full_adder_1 (
    .Carry_In(n1_bit_full_adder_2_carry_out), .A_In(A_In[3]), .B_In(B_In[3]), .Sum_Out(Output[3]),
    .Carry_Out(Carry_Out));
  _1_bit_full_adder u_1_bit_full_adder_2 (
    .Carry_In(n1_bit_full_adder_3_carry_out), .A_In(A_In[2]), .B_In(B_In[2]), .Sum_Out(Output[2]),
    .Carry_Out(n1_bit_full_adder_2_carry_out));
  _1_bit_full_adder u_1_bit_full_adder_3 (
    .Carry_In(n1_bit_full_adder_4_carry_out), .A_In(A_In[1]), .B_In(B_In[1]), .Sum_Out(Output[1]),
    .Carry_Out(n1_bit_full_adder_3_carry_out));
  _1_bit_full_adder u_1_bit_full_adder_4 (
    .Carry_In(Carry_In), .A_In(A_In[0]), .B_In(B_In[0]), .Sum_Out(Output[0]),
    .Carry_Out(n1_bit_full_adder_4_carry_out));
endmodule

// 1-Bit Full\nAdder
module _1_bit_full_adder (
  input  Carry_In,
  input  A_In,
  input  B_In,
  output Sum_Out,
  output Carry_Out
);

  wire n1_bit_half_adder_1_carry_out, n1_bit_half_adder_1_sum_out, n1_bit_half_adder_2_carry_out;

  _1_bit_half_adder u_1_bit_half_adder_1 (
    .A_In(A_In), .B_In(B_In), .Sum_Out(n1_bit_half_adder_1_sum_out), .Carry_Out(n1_bit_half_adder_1_carry_out));
  _1_bit_half_adder u_1_bit_half_adder_2 (
    .A_In(Carry_In), .B_In(n1_bit_half_adder_1_sum_out), .Sum_Out(Sum_Out),
    .Carry_Out(n1_bit_half_adder_2_carry_out));
  or or_1 (Carry_Out, n1_bit_half_adder_2_carry_out, n1_bit_half_adder_1_carry_out);
endmodule

// 4-Bit\nIncrementer
module _4_bit_increment (
  input  [3:0] Input,
  output Carry_Out,
  output [3:0] Output
);

  wire n1_bit_half_adder_2_carry_out, n1_bit_half_adder_3_carry_out, n1_bit_half_adder_4_carry_out;

  _1_bit_half_adder u_1_bit_half_adder_1 (
    .A_In(n1_bit_half_adder_2_carry_out), .B_In(Input[3]), .Sum_Out(Output[3]), .Carry_Out(Carry_Out));
  _1_bit_half_adder u_1_bit_half_adder_2 (
    .A_In(n1_bit_half_adder_3_carry_out), .B_In(Input[2]), .Sum_Out(Output[2]),
    .Carry_Out(n1_bit_half_adder_2_carry_out));
  _1_bit_half_adder u_1_bit_half_adder_3 (
    .A_In(n1_bit_half_adder_4_carry_out), .B_In(Input[1]), .Sum_Out(Output[1]),
    .Carry_Out(n1_bit_half_adder_3_carry_out));
  _1_bit_half_adder u_1_bit_half_adder_4 (
    .A_In(1'b1), .B_In(Input[0]), .Sum_Out(Output[0]), .Carry_Out(n1_bit_half_adder_4_carry_out));
endmodule

// 4-Bit\nDecrementer
module _4_bit_decrementer (
  input  [3:0] Input,
  output Carry_Out,
  output [3:0] Output
);

  wire n1_bit_full_adder_2_carry_out, n1_bit_full_adder_3_carry_out, n1_bit_full_adder_4_carry_out;

  _1_bit_full_adder u_1_bit_full_adder_1 (
    .Carry_In(n1_bit_full_adder_2_carry_out), .A_In(Input[3]), .B_In(1'b1), .Sum_Out(Output[3]),
    .Carry_Out(Carry_Out));
  _1_bit_full_adder u_1_bit_full_adder_2 (
    .Carry_In(n1_bit_full_adder_3_carry_out), .A_In(Input[2]), .B_In(1'b1), .Sum_Out(Output[2]),
    .Carry_Out(n1_bit_full_adder_2_carry_out));
  _1_bit_full_adder u_1_bit_full_adder_3 (
    .Carry_In(n1_bit_full_adder_4_carry_out), .A_In(Input[1]), .B_In(1'b1), .Sum_Out(Output[1]),
    .Carry_Out(n1_bit_full_adder_3_carry_out));
  _1_bit_full_adder u_1_bit_full_adder_4 (
    .Carry_In(1'b0), .A_In(Input[0]), .B_In(1'b1), .Sum_Out(Output[0]),
    .Carry_Out(n1_bit_full_adder_4_carry_out));
endmodule

// 4-Bit\nAND
module _4_bit_and (
  input  [3:0] A_In,
  input  [3:0] B_In,
  output [3:0] Output
);

  and and_1 (Output[3], A_In[3], B_In[3]);
  and and_2 (Output[2], A_In[2], B_In[2]);
  and and_3 (Output[1], A_In[1], B_In[1]);
  and and_4 (Output[0], A_In[0], B_In[0]);
endmodule

// 4-Bit\nOR
module _4_bit_or (
  input  [3:0] A_In,
  input  [3:0] B_In,
  output [3:0] Output
);

  or or_1 (Output[3], A_In[3], B_In[3]);
  or or_2 (Output[2], A_In[2], B_In[2]);
  or or_3 (Output[1], A_In[1], B_In[1]);
  or or_4 (Output[0], A_In[0], B_In[0]);
endmodule

// 4-Bit\nXOR
module _4_bit_xor (
  input  [3:0] A_In,
  input  [3:0] B_In,
  output [3:0] Output
);

  xor xor_1 (Output[3], A_In[3], B_In[3]);
  xor xor_2 (Output[2], A_In[2], B_In[2]);
  xor xor_3 (Output[1], A_In[1], B_In[1]);
  xor xor_4 (Output[0], A_In[0], B_In[0]);
endmodule

// 4-Bit One's\nComplement
module _4_bit_ones_complement (
  input  [3:0] Input,
  output [3:0] Output
);

  not not_1 (Output[3], Input[3]);
  not not_2 (Output[2], Input[2]);
  not not_3 (Output[1], Input[1]);
  not not_4 (Output[0], Input[0]);
endmodule

// 4-Bit\nSubtractor
module _4_bit_subtractor (
  input  [3:0] B_In,
  input  [3:0] A_In,
  output Overflow___Underflow,
  output [3:0] Output
);

  wire n4_bit_full_adder_1_carry_out;
  wire [3:0] n4_bit_ones_complement_1_output;

  xor xor_1 (Overflow___Underflow, n4_bit_full_adder_1_carry_out, 1'b1);
  _4_bit_ones_complement u_4_bit_ones_complement_1 (.Input(B_In), .Output(n4_bit_ones_complement_1_output));
  _4_bit_full_adder u_4_bit_full_adder_1 (
    .A_In(A_In), .B_In(n4_bit_ones_complement_1_output), .Output(Output),
    .Carry_Out(n4_bit_full_adder_1_carry_out), .Carry_In(1'b1));
endmodule

// 4-to-16 Decoder
module _4_to_16_decoder (
  input  Data_In,
  input  [3:0] Address__operation,
  output [15:0] out_3
);

  wire not_1_out, not_2_out, not_3_out, not_4_out;

  not not_1 (not_1_out, Address__operation[0]);
  not not_2 (not_2_out, Address__operation[1]);
  not not_3 (not_3_out, Address__operation[2]);
  not not_4 (not_4_out, Address__operation[3]);
  and and_1 (out_3[0], Data_In, not_1_out, not_2_out, not_3_out, not_4_out);
  and and_2 (out_3[1], Data_In, Address__operation[0], not_2_out, not_3_out, not_4_out);
  and and_3 (out_3[2], Data_In, not_1_out, Address__operation[1], not_3_out, not_4_out);
  and and_4 (out_3[3], Data_In, Address__operation[0], Address__operation[1], not_3_out, not_4_out);
  and and_5 (out_3[4], Data_In, not_1_out, not_2_out, Address__operation[2], not_4_out);
  and and_6 (out_3[5], Data_In, Address__operation[0], not_2_out, Address__operation[2], not_4_out);
  and and_7 (out_3[6], Data_In, not_1_out, Address__operation[1], Address__operation[2], not_4_out);
  and and_8 (out_3[7], Data_In, Address__operation[0], Address__operation[1], Address__operation[2], not_4_out);
  and and_9 (out_3[8], Data_In, not_1_out, not_2_out, not_3_out, Address__operation[3]);
  and and_10 (out_3[9], Data_In, Address__operation[0], not_2_out, not_3_out, Address__operation[3]);
  and and_11 (out_3[10], Data_In, not_1_out, Address__operation[1], not_3_out, Address__operation[3]);
  and and_12 (out_3[11], Data_In, Address__operation[0], Address__operation[1], not_3_out, Address__operation[3]);
  and and_13 (out_3[12], Data_In, not_1_out, not_2_out, Address__operation[2], Address__operation[3]);
  and and_14 (out_3[13], Data_In, Address__operation[0], not_2_out, Address__operation[2], Address__operation[3]);
  and and_15 (out_3[14], Data_In, not_1_out, Address__operation[1], Address__operation[2], Address__operation[3]);
  and and_16 (out_3[15], Data_In, Address__operation[0], Address__operation[1], Address__operation[2], Address__operation[3]);
endmodule

module _1_to_4_splitter (
  input  Data_In
);
endmodule

// 4-Bit\nLeft Shift
module _4_bit_left_shift (
  input  [3:0] Input,
  output [3:0] Output
);

  wire and_1_out, and_2_out, and_3_out, and_4_out, and_5_out, and_6_out, and_7_out, and_8_out, and_9_out,
       and_10_out, and_11_out, and_12_out, not_1_out, not_2_out, not_3_out, not_4_out, not_5_out, not_6_out,
       not_7_out, not_8_out;

  and and_1 (and_1_out, 1'b0, 1'b0);
  not not_1 (not_1_out, 1'b0);
  and and_2 (and_2_out, Input[3], not_1_out, not_2_out);
  or or_1 (Output[3], and_1_out, and_2_out, and_3_out);
  not not_2 (not_2_out, 1'b1);
  and and_3 (and_3_out, 1'b1, Input[2]);
  and and_4 (and_4_out, 1'b0, Input[3]);
  not not_3 (not_3_out, 1'b0);
  and and_5 (and_5_out, Input[2], not_3_out, not_4_out);
  or or_2 (Output[2], and_4_out, and_5_out, and_6_out);
  not not_4 (not_4_out, 1'b1);
  and and_6 (and_6_out, 1'b1, Input[1]);
  and and_7 (and_7_out, 1'b0, Input[2]);
  not not_5 (not_5_out, 1'b0);
  and and_8 (and_8_out, Input[1], not_5_out, not_6_out);
  or or_3 (Output[1], and_7_out, and_8_out, and_9_out);
  not not_6 (not_6_out, 1'b1);
  and and_9 (and_9_out, 1'b1, Input[0]);
  and and_10 (and_10_out, 1'b0, Input[1]);
  not not_7 (not_7_out, 1'b0);
  and and_11 (and_11_out, Input[0], not_7_out, not_8_out);
  or or_4 (Output[0], and_10_out, and_11_out, and_12_out);
  not not_8 (not_8_out, 1'b1);
  and and_12 (and_12_out, 1'b1, 1'b0);

  // Notes on the sheet:
  //   Right Shift
  //   Left Shift
endmodule

// 4-Bit\nRight Shift
module _4_bit_right_shift (
  input  [3:0] Input,
  output [3:0] Output
);

  wire and_1_out, and_2_out, and_3_out, and_4_out, and_5_out, and_6_out, and_7_out, and_8_out, and_9_out,
       and_10_out, and_11_out, and_12_out, not_1_out, not_2_out, not_3_out, not_4_out, not_5_out, not_6_out,
       not_7_out, not_8_out;

  and and_1 (and_1_out, 1'b1, 1'b0);
  not not_1 (not_1_out, 1'b1);
  and and_2 (and_2_out, Input[3], not_1_out, not_2_out);
  or or_1 (Output[3], and_1_out, and_2_out, and_3_out);
  not not_2 (not_2_out, 1'b0);
  and and_3 (and_3_out, 1'b0, Input[2]);
  and and_4 (and_4_out, 1'b1, Input[3]);
  not not_3 (not_3_out, 1'b1);
  and and_5 (and_5_out, Input[2], not_3_out, not_4_out);
  or or_2 (Output[2], and_4_out, and_5_out, and_6_out);
  not not_4 (not_4_out, 1'b0);
  and and_6 (and_6_out, 1'b0, Input[1]);
  and and_7 (and_7_out, 1'b1, Input[2]);
  not not_5 (not_5_out, 1'b1);
  and and_8 (and_8_out, Input[1], not_5_out, not_6_out);
  or or_3 (Output[1], and_7_out, and_8_out, and_9_out);
  not not_6 (not_6_out, 1'b0);
  and and_9 (and_9_out, 1'b0, Input[0]);
  and and_10 (and_10_out, 1'b1, Input[1]);
  not not_7 (not_7_out, 1'b1);
  and and_11 (and_11_out, Input[0], not_7_out, not_8_out);
  or or_4 (Output[0], and_10_out, and_11_out, and_12_out);
  not not_8 (not_8_out, 1'b0);
  and and_12 (and_12_out, 1'b0, 1'b0);

  // Notes on the sheet:
  //   Right Shift
  //   Left Shift
endmodule
